# Fritzing sketch autoconsommation (saved by Fritzing 0.9.3b)
circuit board: 8.46667cm x 5.64444cm
breadboards: 1

parts:
  LCD1 = LCD screen  # not connected
  Arduino = Arduino Nano (Rev3.0)
  LED1 = LED - 5mm [color="Red (633nm)" package="5 mm [THT]"]
  S1 = Pushbutton [package="[THT]"]
  R1 = Resistor [tolerance=±5% resistance=100k package=THT]
  R2 = Resistor [tolerance=±5% resistance=12k package=THT]
  R3 = Trimmer Potentiometer [maximum_resistance=10kΩ package=THT]
  DS1 = DS18B20 1-Wire Temperature Sensor [part_number=DS18B20]
  L5 = Inductor [package="400 mil [THT]"]
  L6 = Inductor [package="400 mil [THT]"]
  L7 = Inductor [package="400 mil [THT]"]
  L8 = Inductor [package="400 mil [THT]"]
  L9 = Inductor [package="400 mil [THT]"]  # not connected
  U1 = POT [package=pot_mammoth]
  R4 = Photocell (LDR) [package=THT]

nets:
  N1: Arduino.GND, S1.Pin_1, S1.Pin_2, R3.leg1, DS1.DQ
  N2: Arduino.D5, LED1.anode
  N3: Arduino.D9, S1.Pin_3, S1.Pin_4
  N4: Arduino.D12/MISO, DS1.GND
  5V: Arduino.5V, DS1.VDD
  N5: Arduino.A3, L7.pin_0
  N6: Arduino.A2, L6.pin_0
  N7: Arduino.A1, L5.pin_0
  N8: Arduino.A0, R1.Pin_1, R2.Pin_0
  N9: Arduino.3V3, R1.Pin_0, L5.pin_1, L6.pin_1, L7.pin_1, L8.pin_0
  N10: LED1.cathode, R3.wiper
  N11: R2.Pin_1, L8.pin_1
  N12: U1.S, R4.pin_1
  N13: U1.A, R4.pin_0
