# Fritzing sketch breadboard_avec_connecteur (saved by Fritzing 0.9.3b)
circuit board: 4.58406cm x 4.5363cm
breadboards: 1

parts:
  Arduino_Nano = Arduino Nano (Rev3.0)
  S1 = Pushbutton [package="[THT]"]
  R1 = Resistor [tolerance=±5% resistance=100k package=THT]
  R2 = Resistor [tolerance=±5% resistance=12k package=THT]
  R3 = Trimmer Potentiometer [maximum_resistance=10kΩ package=THT]
  J1 = female pin header, 3 pins [form="♀ (female)"]
  J2 = female pin header, 2 pins [form="♀ (female)"]
  J3 = female pin header, 4 pins [form="♀ (female)"]
  J4 = female pin header, 2 pins [form="♀ (female)"]
  J5 = female pin header, 2 pins [form="♀ (female)"]
  J6 = female pin header, 2 pins [form="♀ (female)"]
  J7 = female pin header, 2 pins [form="♀ (female)"]

nets:
  N1: Arduino_Nano.GND, S1.Pin_1, S1.Pin_2, R3.leg1, J1.pin3, J3.pin3
  N2: Arduino_Nano.D5, J2.pin1
  N3: Arduino_Nano.D9, S1.Pin_3, S1.Pin_4
  N4: Arduino_Nano.D12/MISO, J1.pin1
  N5: Arduino_Nano.5V, J1.pin2, J3.pin4
  N6: Arduino_Nano.A5, J3.pin2
  N7: Arduino_Nano.A4, J3.pin1
  N8: Arduino_Nano.A3, J6.pin2
  N9: Arduino_Nano.A2, J5.pin2
  N10: Arduino_Nano.A1, J4.pin2
  N11: Arduino_Nano.A0, R1.Pin_1, R2.Pin_0
  N12: Arduino_Nano.3V3, R1.Pin_0, J4.pin1, J5.pin1, J6.pin1, J7.pin1
  N13: R2.Pin_1, J7.pin2
  N14: R3.wiper, J2.pin2

notes:
  J1: Sonde Dallas
  J2: LED
  J3: I2C
  J4,J5,J6: Sonde 1 wire
